# Fritzing sketch Button_led (saved by Fritzing 0.7.7b)
breadboards: 1

parts:
  Arduino2 = Arduino
  R3 = Resistor [tolerance=±5% resistance=220 package=THT]
  PushButton1 = Pushbutton [package="[THT]"]
  LED2 = LED - 5mm [color="Red (633nm)" package="5 mm [THT]"]  # not connected
  R4 = Resistor [tolerance=±5% resistance=10k package=THT]

nets:
  N1: Arduino2.GND, PushButton1.Pin_2
  N2: Arduino2.D13, R3.Pin_1
  N3: Arduino2.D10, PushButton1.Pin_4, R4.Pin_0
  N4: Arduino2.+5V, R4.Pin_1
