# Fritzing sketch DigitalRead_button (saved by Fritzing 0.7.7b)
breadboards: 1

parts:
  Arduino2 = Arduino
  PushButton1 = Pushbutton [package="[THT]"]
  R4 = Resistor [tolerance=±5% resistance=10k package=THT]

nets:
  N1: Arduino2.GND, PushButton1.Pin_2
  N2: Arduino2.D10, PushButton1.Pin_4, R4.Pin_0
  N3: Arduino2.+5V, R4.Pin_1
