# Fritzing sketch led_potentiometer_pwm (saved by Fritzing 0.7.7b)
breadboards: 1

parts:
  LED1 = LED - 5mm [color="Red (633nm)" package="5 mm [THT]"]  # not connected
  Arduino1 = Arduino
  R1 = Rotary Potentiometer (Small) [maximum_resistance=100kΩ]
  R2 = Resistor [tolerance=±5% resistance=220 package=THT]

nets:
  N1: Arduino1.D9, R2.Pin_0
  N2: Arduino1.+5V, R1.leg1
  N3: Arduino1.GND, R1.leg2
  N4: Arduino1.A0, R1.wiper
