# Fritzing sketch PhotoResistor_LED (saved by Fritzing 0.7.7b)
breadboards: 1

parts:
  R1 = Photocell (LDR) [package=THT]
  Arduino1 = Arduino
  R2 = Resistor [tolerance=±5% resistance=10k package=THT]
  LED1 = LED - 5mm [color="Red (633nm)" package="5 mm [THT]"]
  R3 = Resistor [tolerance=±5% resistance=220 package=THT]

nets:
  N1: R1.pin_0, Arduino1.A0, R2.Pin_1
  N2: R1.pin_1, Arduino1.GND, LED1.cathode
  N3: Arduino1.D11, R3.Pin_0
  N4: Arduino1.+5V, R2.Pin_0
  N5: LED1.anode, R3.Pin_1
