# Fritzing sketch Multiple (saved by Fritzing 0.7.7b)
breadboards: 1

parts:
  Arduino2 = Arduino
  R4 = Resistor [tolerance=±5% resistance=10k package=THT]
  R5 = Photocell (LDR) [package=THT]
  R6 = Photocell (LDR) [package=THT]
  R7 = Resistor [tolerance=±5% resistance=10k package=THT]
  R8 = Resistor [tolerance=±5% resistance=10k package=THT]
  R9 = Rotary Potentiometer (Small) [maximum_resistance=100kΩ]

nets:
  N1: Arduino2.+5V, R4.Pin_0, R7.Pin_0, R8.Pin_0
  N2: Arduino2.GND, R5.pin_1, R6.pin_1, R9.leg2
  N3: Arduino2.A0, R4.Pin_1, R5.pin_0
  N4: Arduino2.A1, R6.pin_0, R7.Pin_1
  N5: Arduino2.A2, R9.wiper
  N6: R8.Pin_1, R9.leg1
