# Fritzing sketch Arduino to Processing_range (saved by Fritzing 0.7.7b)
breadboards: 1

parts:
  R1 = Rotary Potentiometer (Small) [maximum_resistance=100kΩ]
  Arduino1 = Arduino

nets:
  N1: R1.leg1, Arduino1.GND
  N2: R1.wiper, Arduino1.A0
  N3: R1.leg2, Arduino1.+5V
