# Fritzing sketch Processing to Arduino Simple LED (saved by Fritzing 0.7.7b)
breadboards: 1

parts:
  Arduino1 = Arduino
  LED3 = LED - 5mm [color="Red (633nm)" package="5 mm [THT]"]
  R3 = Resistor [tolerance=±5% resistance=220 package=THT]

nets:
  N1: Arduino1.D11, R3.Pin_0
  N2: Arduino1.GND, LED3.cathode
  N3: LED3.anode, R3.Pin_1
